// Logisim project 1.dl crc.circ as structural Verilog: 1 circuit, main circuit main
module main (
  input  A,
  input  B,
  input  A_2,
  input  B_2,
  input  A_3,
  input  A_4,
  input  B_3,
  input  A_5,
  input  B_4,
  output Y1,
  output Y2,
  output Y3,
  output Y4,
  output Y5
);

  and and_1 (Y1, A, B);
  or or_1 (Y2, A_2, B_2);
  not not_1 (Y3, A_3);
  xor xor_1 (Y4, A_4, B_3);
  xnor xnor_1 (Y5, A_5, B_4);
endmodule
