// Logisim project 11.circ as structural Verilog: 1 circuit, main circuit main
module main (
  input  in_1,
  input  in_2,
  input  in_3,
  input  in_4,
  input  in_5,
  input  in_6,
  input  [1:0] in_7,
  output out_8
);

  wire not_1_out, not_2_out, not_3_out;

  not not_1 (not_1_out, in_1);
  not not_2 (not_2_out, in_2);
  // AND_Gate and_1 has open pins: in0=in_1, out=open
  // AND_Gate and_2 is placed but not wired
  // AND_Gate and_3 is placed but not wired
  // AND_Gate and_4 is placed but not wired
  not not_3 (not_3_out, in_4);
  Multiplexer #(.select(2)) multiplexer_1 (
    .in0(in_3), .in1(not_3_out), .in2(in_5), .in3(in_6), .out(out_8), .sel(in_7));  // open: en
endmodule
