// Logisim project 5.dl.crc.circ as structural Verilog: 1 circuit, main circuit main
module main (
  input  in_1,
  input  in_2,
  input  in_3,
  input  in_4,
  input  in_5,
  input  in_6,
  output out_7,
  output out_8
);

  wire and_1_out, and_2_out, and_3_out, and_4_out, and_5_out, and_6_out, not_1_out, not_2_out, not_3_out,
       not_4_out;

  not not_1 (not_1_out, in_1);
  not not_2 (not_2_out, in_4);
  not not_3 (not_3_out, in_1);
  not not_4 (not_4_out, in_3);
  and and_1 (and_1_out, not_2_out, in_5);
  or or_1 (out_8, and_1_out, in_6);
  and and_2 (and_2_out, not_1_out, not_3_out, in_3);
  and and_3 (and_3_out, not_1_out, in_1, not_4_out);
  and and_4 (and_4_out, not_1_out, in_1, in_3);
  and and_5 (and_5_out, in_1, not_3_out, in_3);
  and and_6 (and_6_out, in_1, in_1, in_3);
  or or_2 (out_7, and_2_out, and_3_out, and_4_out, and_5_out, and_6_out);

  assign in_2 = in_1;
endmodule
